# Fritzing sketch DesainTugas1&2 (saved by Fritzing 0.9.3b)
breadboards: 1

parts:
  Mod1 = KY-018 Photoresistor Module [package="Breakout board"]
  U1 = NodeMCU V1.0
  DHT1 = DHT11 Humitidy and Temperature Sensor
  LED1 = LED - 5mm [color="Red (633nm)" package="5 mm [THT]"]
  LED2 = LED - 5mm [color="Blue (430nm)" package="5 mm [THT]"]
  LED3 = LED - 5mm [color="White (4500K)" package="5 mm [THT]"]
  R1 = Resistor [tolerance=±5% resistance=220 package=THT]
  R2 = Resistor [tolerance=±5% resistance=220 package=THT]
  R3 = Resistor [tolerance=±5% resistance=220 package=THT]

nets:
  VIN: Mod1.S, U1.Vin, DHT1.VDD
  N1: Mod1.Vin, U1.A0
  N2: U1.D0, R1.Pin_1
  N3: U1.D1, DHT1.DATA
  N4: U1.D2, R2.Pin_1
  N5: U1.D3, R3.Pin_1
  GND: U1.GND, DHT1.GND
  N6: LED1.cathode, R1.Pin_0
  N7: LED1.anode, LED2.anode, LED3.anode
  N8: LED2.cathode, R2.Pin_0
  N9: LED3.cathode, R3.Pin_0

custom parts:
  KY-018 Photoresistor Module: KY-018 Photoresistor module, used to measure light intensity. It can determine the presence or absence of light.
  NodeMCU V1.0: ESP8266 based NodeMCU
  DHT11 Humitidy and Temperature Sensor: DHT11 Humidity and Temperature Sensor
